// Logisim project ETFStudent.circ as structural Verilog: 16 circuits, main circuit REG32_LD
module REG32_LD (
  input  [31:0] I15__0,
  input  LD,
  input  mr,
  input  CLK,
  output [31:0] A15__0
);

  REG16_LD reg16_ld_1 (.I15__0(I15__0[31:16]), .LD(LD), .CLK(CLK), .A15__0(A15__0[31:16]), .mr(mr));
  REG16_LD reg16_ld_2 (.I15__0(I15__0[15:0]), .LD(LD), .CLK(CLK), .A15__0(A15__0[15:0]), .mr(mr));

  // Notes on the sheet:
  //   __
endmodule

module KMADR (
  input  immed,
  input  memdir,
  input  regdir,
  input  regind,
  input  pcrel,
  output [3:0] Adr3__0
);

  assign Adr3__0 = immed ? 4'b0010 : 4'bz;  // Controlled_Buffer controlled_buffer_1
  assign Adr3__0 = memdir ? 4'b0011 : 4'bz;  // Controlled_Buffer controlled_buffer_2
  assign Adr3__0 = regdir ? 4'b0100 : 4'bz;  // Controlled_Buffer controlled_buffer_3
  assign Adr3__0 = regind ? 4'b0110 : 4'bz;  // Controlled_Buffer controlled_buffer_4
  assign Adr3__0 = pcrel ? 4'b0111 : 4'bz;  // Controlled_Buffer controlled_buffer_5
endmodule

module KMOPR (
  input  LD,
  input  ST,
  input  ADD,
  input  AND,
  input  SWAP,
  input  JADR,
  input  OR,
  input  HALT,
  input  BX,
  input  BR,
  input  JLEQ,
  input  JMP,
  input  JSR,
  input  POP_RTS,
  input  ASL,
  input  STIVTP,
  input  PUSH,
  input  ABS,
  input  RTI,
  output [5:0] Adr5__0
);

  assign Adr5__0 = LD ? 6'b000010 : 6'bz;  // Controlled_Buffer controlled_buffer_1
  assign Adr5__0 = ST ? 6'b000100 : 6'bz;  // Controlled_Buffer controlled_buffer_2
  assign Adr5__0 = ADD ? 6'b001100 : 6'bz;  // Controlled_Buffer controlled_buffer_3
  assign Adr5__0 = AND ? 6'b001101 : 6'bz;  // Controlled_Buffer controlled_buffer_4
  assign Adr5__0 = SWAP ? 6'b001110 : 6'bz;  // Controlled_Buffer controlled_buffer_5
  assign Adr5__0 = JADR ? 6'b010000 : 6'bz;  // Controlled_Buffer controlled_buffer_6
  assign Adr5__0 = OR ? 6'b010001 : 6'bz;  // Controlled_Buffer controlled_buffer_7
  assign Adr5__0 = HALT ? 6'b010010 : 6'bz;  // Controlled_Buffer controlled_buffer_8
  assign Adr5__0 = BX ? 6'b010011 : 6'bz;  // Controlled_Buffer controlled_buffer_9
  assign Adr5__0 = BR ? 6'b010100 : 6'bz;  // Controlled_Buffer controlled_buffer_10
  assign Adr5__0 = JLEQ ? 6'b010101 : 6'bz;  // Controlled_Buffer controlled_buffer_11
  assign Adr5__0 = JMP ? 6'b010110 : 6'bz;  // Controlled_Buffer controlled_buffer_12
  assign Adr5__0 = JSR ? 6'b010111 : 6'bz;  // Controlled_Buffer controlled_buffer_13
  assign Adr5__0 = POP_RTS ? 6'b011101 : 6'bz;  // Controlled_Buffer controlled_buffer_14
  assign Adr5__0 = ASL ? 6'b100101 : 6'bz;  // Controlled_Buffer controlled_buffer_15
  assign Adr5__0 = STIVTP ? 6'b100110 : 6'bz;  // Controlled_Buffer controlled_buffer_16
  assign Adr5__0 = PUSH ? 6'b100111 : 6'bz;  // Controlled_Buffer controlled_buffer_17
  assign Adr5__0 = ABS ? 6'b101101 : 6'bz;  // Controlled_Buffer controlled_buffer_18
  assign Adr5__0 = RTI ? 6'b101110 : 6'bz;  // Controlled_Buffer controlled_buffer_19
endmodule

module REG6_INC_LD (
  input  [5:0] I5__0,
  input  LD,
  input  INC,
  input  mr,
  input  CLK,
  output [5:0] A5__0
);

  wire reg2m_inc_ld_2_cout, reg2m_inc_ld_3_cout;

  REG2m_INC_LD reg2m_inc_ld_1 (
    .I1__0(I5__0[5:4]), .LD(LD), .Cin(reg2m_inc_ld_2_cout), .INC(INC), .CLK(CLK), .A1__0(A5__0[5:4]), .mr(mr));  // open: Cout
  REG2m_INC_LD reg2m_inc_ld_2 (
    .I1__0(I5__0[3:2]), .LD(LD), .Cin(reg2m_inc_ld_3_cout), .INC(INC), .CLK(CLK), .Cout(reg2m_inc_ld_2_cout),
    .A1__0(A5__0[3:2]), .mr(mr));
  REG2m_INC_LD reg2m_inc_ld_3 (
    .I1__0(I5__0[1:0]), .LD(LD), .Cin(INC), .INC(INC), .CLK(CLK), .Cout(reg2m_inc_ld_3_cout),
    .A1__0(A5__0[1:0]), .mr(mr));

  // Notes on the sheet:
  //   __
endmodule

module ROM32X24 (
  input  [4:0] A4__0,
  input  CS,
  output [23:0] DOUT
);

  ROM #(.addrWidth(5), .dataWidth(24)) rom_1 (.addr(A4__0), .data(DOUT), .sel(CS));
endmodule

module ROM15X20 (
  input  [3:0] A3__0,
  input  CS,
  output [19:0] DOUT
);

  ROM #(.addrWidth(4), .dataWidth(20)) rom_1 (.addr(A3__0), .data(DOUT), .sel(CS));
endmodule

module REG1m_INC_DEC_LD (
  input  Ii,
  input  LD,
  input  DEC,
  input  Ei,
  input  INC,
  input  Ci,
  input  CLK,
  input  mr,
  output Ai,
  output Eout,
  output Cout
);

  wire and_1_out, and_2_out, and_3_out, and_4_out, or_1_out, xor_1_out, xor_2_out;

  Pull_Resistor pull_resistor_1 (.node(Ci));
  Pull_Resistor pull_resistor_2 (.node(LD));
  Pull_Resistor pull_resistor_3 (.node(Ei));
  Pull_Resistor pull_resistor_4 (.node(Ii));
  xor xor_1 (xor_1_out, Ei, Ai);
  xor xor_2 (xor_2_out, Ci, Ai);
  Pull_Resistor #(.pull(1)) pull_resistor_5 (.node(mr));
  Pull_Resistor pull_resistor_6 (.node(DEC));
  and and_1 (and_1_out, DEC, xor_1_out);
  and and_2 (and_2_out, INC, xor_2_out);
  and and_3 (and_3_out, Ii, LD);
  and and_4 (and_4_out, ~LD, ~DEC, ~INC, Ai);  // AND_Gate
  or or_1 (or_1_out, and_3_out, and_4_out, and_1_out, and_2_out);
  DFF dff_1 (.CLK(CLK), .D(or_1_out), .Rd(mr), .Q(Ai));  // open: Sd, notQ
  and and_5 (Eout, ~Ai, Ei);  // AND_Gate
  and and_6 (Cout, Ai, Ci);

  // Notes on the sheet:
  //   __
endmodule

module REG2m_INC_DEC_LD (
  input  [1:0] I1__0,
  input  LD,
  input  Ein,
  input  DEC,
  input  Cin,
  input  INC,
  input  mr,
  input  CLK,
  output Eout,
  output Cout,
  output [1:0] A1__0
);

  wire reg1m_inc_dec_ld_2_cout, reg1m_inc_dec_ld_2_eout;

  REG1m_INC_DEC_LD reg1m_inc_dec_ld_1 (
    .Ii(I1__0[1]), .LD(LD), .DEC(DEC), .Ei(reg1m_inc_dec_ld_2_eout), .INC(INC), .Ci(reg1m_inc_dec_ld_2_cout),
    .CLK(CLK), .mr(mr), .Ai(A1__0[1]), .Eout(Eout), .Cout(Cout));
  REG1m_INC_DEC_LD reg1m_inc_dec_ld_2 (
    .Ii(I1__0[0]), .LD(LD), .DEC(DEC), .Ei(Ein), .INC(INC), .Ci(Cin), .CLK(CLK), .mr(mr), .Ai(A1__0[0]),
    .Eout(reg1m_inc_dec_ld_2_eout), .Cout(reg1m_inc_dec_ld_2_cout));

  // Notes on the sheet:
  //   __
endmodule

module REG4m_INC_DEC_LD (
  input  [3:0] I3__0,
  input  LD,
  input  Ein,
  input  DEC,
  input  Cin,
  input  INC,
  input  mr,
  input  CLK,
  output Eout,
  output Cout,
  output [3:0] A3__0
);

  wire reg2m_inc_dec_ld_2_cout, reg2m_inc_dec_ld_2_eout;

  REG2m_INC_DEC_LD reg2m_inc_dec_ld_1 (
    .I1__0(I3__0[3:2]), .LD(LD), .Ein(reg2m_inc_dec_ld_2_eout), .DEC(DEC), .Cin(reg2m_inc_dec_ld_2_cout),
    .INC(INC), .mr(mr), .CLK(CLK), .Eout(Eout), .Cout(Cout), .A1__0(A3__0[3:2]));
  REG2m_INC_DEC_LD reg2m_inc_dec_ld_2 (
    .I1__0(I3__0[1:0]), .LD(LD), .Ein(Ein), .DEC(DEC), .Cin(Cin), .INC(INC), .mr(mr), .CLK(CLK),
    .Eout(reg2m_inc_dec_ld_2_eout), .Cout(reg2m_inc_dec_ld_2_cout), .A1__0(A3__0[1:0]));

  // Notes on the sheet:
  //   __
endmodule

module REG8m_INC_DEC_LD (
  input  [7:0] I7__0,
  input  LD,
  input  Ein,
  input  DEC,
  input  Cin,
  input  INC,
  input  mr,
  input  CLK,
  output Eout,
  output Cout,
  output [7:0] A7__0
);

  wire reg4m_inc_dec_ld_2_cout, reg4m_inc_dec_ld_2_eout;

  REG4m_INC_DEC_LD reg4m_inc_dec_ld_1 (
    .I3__0(I7__0[7:4]), .LD(LD), .Ein(reg4m_inc_dec_ld_2_eout), .DEC(DEC), .Cin(reg4m_inc_dec_ld_2_cout),
    .INC(INC), .mr(mr), .CLK(CLK), .Eout(Eout), .Cout(Cout), .A3__0(A7__0[7:4]));
  REG4m_INC_DEC_LD reg4m_inc_dec_ld_2 (
    .I3__0(I7__0[3:0]), .LD(LD), .Ein(Ein), .DEC(DEC), .Cin(Cin), .INC(INC), .mr(mr), .CLK(CLK),
    .Eout(reg4m_inc_dec_ld_2_eout), .Cout(reg4m_inc_dec_ld_2_cout), .A3__0(A7__0[3:0]));

  // Notes on the sheet:
  //   __
endmodule

module REG16m_INC_DEC_LD (
  input  [15:0] I15__0,
  input  LD,
  input  Ein,
  input  DEC,
  input  Cin,
  input  INC,
  input  mr,
  input  CLK,
  output Eout,
  output Cout,
  output [15:0] A15__0
);

  wire reg8m_inc_dec_ld_2_cout, reg8m_inc_dec_ld_2_eout;

  REG8m_INC_DEC_LD reg8m_inc_dec_ld_1 (
    .I7__0(I15__0[15:8]), .LD(LD), .Ein(reg8m_inc_dec_ld_2_eout), .DEC(DEC), .Cin(reg8m_inc_dec_ld_2_cout),
    .INC(INC), .mr(mr), .CLK(CLK), .Eout(Eout), .Cout(Cout), .A7__0(A15__0[15:8]));
  REG8m_INC_DEC_LD reg8m_inc_dec_ld_2 (
    .I7__0(I15__0[7:0]), .LD(LD), .Ein(Ein), .DEC(DEC), .Cin(Cin), .INC(INC), .mr(mr), .CLK(CLK),
    .Eout(reg8m_inc_dec_ld_2_eout), .Cout(reg8m_inc_dec_ld_2_cout), .A7__0(A15__0[7:0]));

  // Notes on the sheet:
  //   __
endmodule

module REG16_INC_DEC_LD (
  input  [15:0] I15__0,
  input  LD,
  input  DEC,
  input  INC,
  input  mr,
  input  CLK,
  output [15:0] A15__0
);

  REG16m_INC_DEC_LD reg16m_inc_dec_ld_1 (
    .I15__0(I15__0), .LD(LD), .Ein(DEC), .DEC(DEC), .Cin(INC), .INC(INC), .mr(mr), .CLK(CLK), .A15__0(A15__0));  // open: Eout, Cout

  // Notes on the sheet:
  //   __
endmodule

module ROM15X21 (
  input  [3:0] A3__0,
  input  CS,
  output [20:0] DOUT
);

  ROM #(.addrWidth(4), .dataWidth(21)) rom_1 (.addr(A3__0), .data(DOUT), .sel(CS));
endmodule

module ALU16b (
  input  Cin,
  input  [15:0] A,
  input  [15:0] B,
  input  add,
  input  \and ,
  input  sub,
  input  \or ,
  input  abs,
  output [15:0] F,
  output Cout
);

  wire adder_1_cout, subtractor_1_bout;
  wire [15:0] adder_1_out, and_1_out, inc16_1_f, multiplexer_1_out, not_1_out, or_1_out, subtractor_1_out;

  assign not_1_out = ~A;  // NOT_Gate not_1, 16 bits wide
  INC16 inc16_1 (.Cin(1'b1), .A(not_1_out), .F(inc16_1_f));  // open: Cout
  Adder #(.width(16)) adder_1 (.a(A), .b(B), .out(adder_1_out), .cin(Cin), .cout(adder_1_cout));
  Subtractor #(.width(16)) subtractor_1 (.a(A), .b(B), .out(subtractor_1_out), .bin(Cin), .bout(subtractor_1_bout));
  Multiplexer #(.width(16), .enable("false")) multiplexer_1 (
    .in0(A), .in1(inc16_1_f), .out(multiplexer_1_out), .sel(A[15]));
  assign F = add ? adder_1_out : 16'bz;  // Controlled_Buffer controlled_buffer_1
  assign Cout = add ? adder_1_cout : 1'bz;  // Controlled_Buffer controlled_buffer_2
  assign F = sub ? subtractor_1_out : 16'bz;  // Controlled_Buffer controlled_buffer_3
  assign Cout = sub ? subtractor_1_bout : 1'bz;  // Controlled_Buffer controlled_buffer_4
  assign F = abs ? multiplexer_1_out : 16'bz;  // Controlled_Buffer controlled_buffer_5
  assign and_1_out = A & B;  // AND_Gate and_1, 16 bits wide
  assign or_1_out = A | B;  // OR_Gate or_1, 16 bits wide
  assign F = \and  ? and_1_out : 16'bz;  // Controlled_Buffer controlled_buffer_6
  assign F = \or  ? or_1_out : 16'bz;  // Controlled_Buffer controlled_buffer_7
endmodule

module ROM64X47 (
  input  [5:0] A5__0,
  input  CS,
  output [31:0] DOUT31__0,
  output [14:0] DOUT46__32
);

  ROM #(.addrWidth(6), .dataWidth(15)) rom_1 (.addr(A5__0), .data(DOUT46__32), .sel(CS));
  ROM #(.addrWidth(6), .dataWidth(32)) rom_2 (.addr(A5__0), .data(DOUT31__0), .sel(CS));
endmodule

module ROM32X31 (
  input  [4:0] A4__0,
  input  CS,
  output [30:0] DOUT
);

  ROM #(.addrWidth(5), .dataWidth(31)) rom_1 (.addr(A4__0), .data(DOUT), .sel(CS));
endmodule
