// Logisim project ORT2Project.circ as structural Verilog: 8 circuits, main circuit COMPUTER
module COMPUTER (
);

  wire BTN_RST_out, CLK, cpu_1_inta, interrupt_interface_4_1_p4, interrupt_interface_4_1_p5,
       interrupt_interface_4_1_p6, interrupt_interface_4_1_p7, pull_resistor_2_node, pull_resistor_5_node,
       ram_1_out_8, rst;
  wire [1:0] cpu_1_uext1__0;
  wire [3:0] interrupt_interface_4_1_p1;
  wire [7:0] pull_resistor_3_node, ram_1_out_7;
  wire [15:0] pull_resistor_4_node;

  Button BTN_RST (.out(BTN_RST_out));
  Clock u_CLK (.out(CLK));
  RisingEdge risingedge_1 (.INPUT(BTN_RST_out), .CLK(CLK), .OUTPUT(rst));
  RAM ram_1 (
    .in_1(pull_resistor_4_node), .in_2(CLK), .in_3(pull_resistor_3_node), .in_4(pull_resistor_2_node),
    .in_5(pull_resistor_5_node), .in_6(rst), .out_7(ram_1_out_7), .out_8(ram_1_out_8));
  Pull_Resistor pull_resistor_1 (.node(ram_1_out_7));
  Pull_Resistor pull_resistor_2 (.node(pull_resistor_2_node));
  Pull_Resistor pull_resistor_3 (.node(pull_resistor_3_node));
  Pull_Resistor pull_resistor_4 (.node(pull_resistor_4_node));
  Pull_Resistor pull_resistor_5 (.node(pull_resistor_5_node));
  Pull_Resistor pull_resistor_6 (.node(ram_1_out_8));
  CPU cpu_1 (
    .in_1(rst), .in_2(CLK), .in_3(ram_1_out_8), .in_4(ram_1_out_7), .ABUS(pull_resistor_4_node),
    .DOUTBUS(pull_resistor_3_node), .out_8(pull_resistor_2_node), .out_9(pull_resistor_5_node),
    .inta(cpu_1_inta), .intr3__0(interrupt_interface_4_1_p1), .UEXT1__0(cpu_1_uext1__0));
  // INTERRUPT_INTERFACE_4 interrupt_interface_4_1: pin names not known; wires that end beside it: interrupt_interface_4_1_p1, cpu_1_inta, cpu_1_uext1__0, interrupt_interface_4_1_p4, interrupt_interface_4_1_p5, interrupt_interface_4_1_p6, interrupt_interface_4_1_p7, CLK
  Button BTN_INTR3 (.out(interrupt_interface_4_1_p4));
  Button BTN_INTR2 (.out(interrupt_interface_4_1_p5));
  Button BTN_INTR1 (.out(interrupt_interface_4_1_p6));
  Button BTN_INTR0 (.out(interrupt_interface_4_1_p7));
endmodule

module CPU (
  input  in_1,
  input  in_2,
  input  in_3,
  input  [7:0] in_4,
  input  [3:0] intr3__0,
  output [15:0] ABUS,
  output [7:0] DOUTBUS,
  output out_8,
  output out_9,
  output inta,
  output [1:0] UEXT1__0
);

  wire C16;
  wire [1:0] BR;
  wire [3:0] common_1_phaseffbus;
  wire [4:0] common_1_addrbus;
  wire [6:0] pull_resistor_1_node;
  wire [7:0] pull_resistor_5_node;
  wire [15:0] A, ALU, B, INTRADDR, IVTP, PSW;
  wire [22:0] common_1_instrucbus;
  wire [23:0] pull_resistor_4_node, pull_resistor_7_node;

  COMMON common_1 (
    .CLK(in_2), .RST(in_1), .DIN(in_4), .CMEMBUS(pull_resistor_7_node), .MAR(ABUS), .MDR(DOUTBUS),
    .PHASEFFBUS(common_1_phaseffbus), .INSTRUCBUS(common_1_instrucbus), .ADDRBUS(common_1_addrbus),
    .PSW(PSW), .CREGBUS(pull_resistor_4_node), .CFFBUS(pull_resistor_5_node), .B(B), .A(A),
    .CPSW(pull_resistor_1_node), .ALU(ALU), .IVTPPDSP(INTRADDR), .IVTP15__0(IVTP), .BR(BR), .C16(C16));
  Pull_Resistor pull_resistor_1 (.node(pull_resistor_1_node));
  Pull_Resistor pull_resistor_2 (.node(common_1_phaseffbus));
  Pull_Resistor pull_resistor_3 (.node(common_1_instrucbus));
  Pull_Resistor pull_resistor_4 (.node(pull_resistor_4_node));
  Pull_Resistor pull_resistor_5 (.node(pull_resistor_5_node));
  Pull_Resistor pull_resistor_6 (.node(common_1_addrbus));
  Pull_Resistor pull_resistor_7 (.node(pull_resistor_7_node));
  FETCH fetch_1 (
    .in_1(in_1), .in_2(in_2), .in_3(in_3), .PHASEFFBUS(common_1_phaseffbus),
    .INSTRUCBUS(common_1_instrucbus), .ADDRBUS(common_1_addrbus), .PSW(PSW), .rdMEM(out_9),
    .CMEMBUS(pull_resistor_7_node), .CFFBUS(pull_resistor_5_node), .CREGBUS(pull_resistor_4_node));
  ADDR addr_1 (
    .in_1(in_1), .in_2(in_2), .in_3(in_3), .PHASEFFBUS(common_1_phaseffbus), .ADDRBUS(common_1_addrbus),
    .rdMEM(out_9), .CMEMBUS(pull_resistor_7_node), .CFFBUS(pull_resistor_5_node),
    .CREGBUS(pull_resistor_4_node), .INSTRUCBUS(common_1_instrucbus));
  EXEC exec_1 (
    .in_2(in_1), .in_3(in_2), .in_4(in_3), .B(B), .PHASEFFBUS(common_1_phaseffbus),
    .INSTRUCBUS(common_1_instrucbus), .ADDRBUS(common_1_addrbus), .PSW(PSW), .A(A), .ALU(ALU),
    .CMEMBUS(pull_resistor_7_node), .CFFBUS(pull_resistor_5_node), .CREGBUS(pull_resistor_4_node),
    .CPSW(pull_resistor_1_node), .rdMEM(out_9), .wrMEM(out_8), .DW(BR), .C16(C16));
  INTR intr_1 (
    .in_1(in_1), .in_2(in_2), .in_3(in_3), .PHASEFFBUS(common_1_phaseffbus),
    .INSTRUCBUS(common_1_instrucbus), .PSW(PSW), .intr(intr3__0), .ADDIVTP(INTRADDR),
    .CMEMBUS(pull_resistor_7_node), .CFFBUS(pull_resistor_5_node), .CREGBUS(pull_resistor_4_node),
    .rdMEM(out_9), .wrMEM(out_8), .UEXT1__0(UEXT1__0), .inta(inta), .IVTP(IVTP), .DW(BR));

  // Other names for the same wires on the sheet: CLK = in_2; DIN7__0[7:0] = in_4; FCBUS = in_3; MAR[15:0] = ABUS;
  //   MDR[7:0] = DOUTBUS; RD = out_9; rst = in_1; WR = out_8
endmodule

module COMMON (
  input  CLK,
  input  RST,
  input  [7:0] DIN,
  input  [15:0] ALU,
  input  [15:0] IVTPPDSP,
  input  [23:0] CMEMBUS,
  input  [7:0] CFFBUS,
  input  [23:0] CREGBUS,
  input  [6:0] CPSW,
  input  C16,
  output [15:0] MAR,
  output [15:0] A,
  output [7:0] MDR,
  output [3:0] PHASEFFBUS,
  output [15:0] IVTP15__0,
  output [22:0] INSTRUCBUS,
  output [4:0] ADDRBUS,
  output [15:0] PSW,
  output [15:0] B,
  output [1:0] BR
);

  wire addrinst, and_3_out, and_4_out, and_5_out, and_6_out, and_7_out, and_8_out, and_9_out, and_10_out,
       and_11_out, and_12_out, and_13_out, and_14_out, and_15_out, and_16_out, and_17_out, and_18_out,
       and_19_out, and_20_out, and_21_out, and_22_out, and_23_out, and_24_out, and_25_out, and_26_out,
       and_27_out, and_28_out, and_29_out, and_30_out, and_31_out, and_32_out, and_33_out, and_34_out,
       and_35_out, and_36_out, and_37_out, bezaddrinst, branchinst, dc3_8_3_d7, immed, jmpinst, memcheck,
       memdir, not_1_out, not_2_out, not_3_out, not_4_out, not_5_out, not_6_out, not_7_out, not_8_out,
       not_9_out, not_10_out, not_11_out, not_12_out, or_1_out, or_2_out, or_4_out, or_5_out, or_6_out,
       or_7_out, or_8_out, or_9_out, or_10_out, or_11_out, or_12_out, or_13_out, pcrel, regdir, regind,
       UPDATE, ZCheck;
  wire [2:0] multiplexer_2_out;
  wire [3:0] IR19__16;
  wire [7:0] GPR7__0, IR7__0, IR15__8, IR31__24, mp8_8b_1_y, multiplexer_1_out;
  wire [7:4] IR23__16;
  wire [15:0] ADDJMPREL15__0, ADDPCREL15__0, DW15__0, mp2_16b_1_out_5, mp2_16b_2_out_5, mp2_16b_3_out_5,
       mp4_16b_1_y, mp4_16b_2_y, mp4_16b_3_y, mp8_16b_1_y, PC15__0, SP15__0;
  wire [15:8] GPR15__0;

  // Probe on IR31__24
  REG8_LD reg8_ld_1 (.I7__0(MDR), .LD(CREGBUS[7]), .CLK(CLK), .A7__0(IR31__24));  // open: mr
  // Probe on MAR
  // Probe on {IR23__16, IR19__16}
  MP8_16b mp8_16b_1 (
    .En(1'b1), .S0(CMEMBUS[5]), .S1(CMEMBUS[6]), .S2(CMEMBUS[7]), .I0(PC15__0), .I1({IR15__8, IR7__0}),
    .I2({GPR15__0, GPR7__0}), .I3(ADDPCREL15__0), .I4(SP15__0), .I5(IVTPPDSP), .Y(mp8_16b_1_y));  // open: I6, I7
  REG16_INC_DEC_LD reg16_inc_dec_ld_1 (
    .I15__0(mp8_16b_1_y), .LD(CMEMBUS[0]), .DEC(CMEMBUS[8]), .INC(CMEMBUS[1]), .CLK(CLK), .A15__0(MAR));  // open: mr
  REG8_LD reg8_ld_2 (.I7__0(MDR), .LD(CREGBUS[6]), .CLK(CLK), .A7__0({IR23__16, IR19__16}));  // open: mr
  // Probe on ADDPCREL15__0
  // Probe on A
  and and_1 (ZCheck, ~IR31__24[7], ~IR31__24[6]);  // AND_Gate
  and and_2 (addrinst, ~IR31__24[6], IR31__24[7], IR31__24[4], IR31__24[5], PSW[0]);  // AND_Gate
  and and_3 (and_3_out, ~IR31__24[2], ~IR31__24[3], jmpinst);  // AND_Gate
  DC2_4 dc2_4_1 (
    .En(and_3_out), .X1__0(IR31__24[1:0]), .D0(INSTRUCBUS[13]), .D1(INSTRUCBUS[14]), .D2(INSTRUCBUS[15]));  // open: D3
  MP4_16b mp4_16b_1 (
    .En(1'b1), .S0(CREGBUS[1]), .S1(CREGBUS[2]), .I0(DW15__0), .I1({IR15__8, IR7__0}),
    .I2({GPR15__0, GPR7__0}), .Y(mp4_16b_1_y));  // open: I3
  REG16_LD reg16_ld_1 (.I15__0(mp4_16b_1_y), .LD(CREGBUS[0]), .CLK(CLK), .A15__0(B));  // open: mr
  // Probe on B
  ADD16 add16_1 (.C0(1'b0), .A({{13{IR19__16[3]}}, IR19__16[2:0]}), .B(PC15__0), .F(ADDPCREL15__0));  // open: C16
  MP4_16b mp4_16b_2 (
    .S0(CREGBUS[14]), .S1(CREGBUS[15]), .I0(B), .I1(ALU), .I2(DW15__0), .Y(mp4_16b_2_y));  // open: En, I3
  not not_1 (not_1_out, RST);
  REG16 reg16_1 (
    .LD(CREGBUS[12]), .A(mp4_16b_2_y), .SL(CREGBUS[13]), .IL(1'b0), .CLK(CLK), .I(A), .mr(not_1_out));  // open: CL, SR, IR, DEC, INC, Cout, Eout
  // Probe on IR15__8
  and and_4 (and_4_out, ~IR23__16[7], addrinst);  // AND_Gate
  DC3_8 dc3_8_1 (
    .En(and_4_out), .X2__0(IR23__16[6:4]), .D0(immed), .D1(memdir), .D2(regdir), .D3(regind), .D4(pcrel));  // open: D5, D6, D7
  REG8_LD reg8_ld_3 (.I7__0(MDR), .LD(CREGBUS[5]), .CLK(CLK), .A7__0(IR15__8));  // open: mr
  // Probe on MDR
  REG8_LD reg8_ld_4 (.I7__0(MDR), .LD(CREGBUS[9]), .CLK(CLK), .A7__0(DW15__0[15:8]));  // open: mr
  // Probe on DW15__0[15:8]
  ADD16 add16_2 (
    .C0(1'b0), .A({{9{IR23__16[7]}}, IR23__16[6:4], IR19__16}), .B(PC15__0), .F(ADDJMPREL15__0));  // open: C16
  // Probe on ADDJMPREL15__0
  MP8_8b mp8_8b_1 (
    .En(1'b1), .S0(CMEMBUS[9]), .S1(CMEMBUS[10]), .S2(CMEMBUS[11]), .I0(DIN), .I1(A[15:8]), .I2(A[7:0]),
    .I3(PC15__0[15:8]), .I4(PC15__0[7:0]), .I5({PSW[15], {7{1'b0}}}), .I6({3'b000, PSW[4:0]}),
    .I7(multiplexer_1_out), .Y(mp8_8b_1_y));
  REG8_LD reg8_ld_5 (.I7__0(mp8_8b_1_y), .LD(CMEMBUS[2]), .CLK(CLK), .A7__0(MDR));  // open: mr
  // Probe on IR7__0
  and and_5 (and_5_out, ZCheck, PSW[0]);
  DC2_4 dc2_4_2 (.En(and_5_out), .X1__0(IR31__24[5:4]), .D0(bezaddrinst), .D1(branchinst), .D2(jmpinst));  // open: D3
  and and_6 (and_6_out, ~IR31__24[3], branchinst);  // AND_Gate
  DC3_8 dc3_8_2 (
    .En(and_6_out), .X2__0(IR31__24[2:0]), .D0(INSTRUCBUS[8]), .D1(INSTRUCBUS[9]), .D2(INSTRUCBUS[10]),
    .D3(INSTRUCBUS[11]), .D4(INSTRUCBUS[12]));  // open: D5, D6, D7
  Multiplexer #(.width(8), .enable("false")) multiplexer_1 (
    .in0(GPR15__0), .in1(GPR7__0), .out(multiplexer_1_out), .sel(CMEMBUS[16]));
  REG8_LD reg8_ld_6 (.I7__0(MDR), .LD(CREGBUS[4]), .CLK(CLK), .A7__0(IR7__0));  // open: mr
  or or_1 (or_1_out, immed, memdir);
  or or_2 (or_2_out, regdir, regind);
  // Probe on DW15__0[7:0]
  and and_7 (and_7_out, ~IR19__16[0], ~IR19__16[1], ~IR19__16[2], ~IR19__16[3]);  // AND_Gate
  and and_8 (and_8_out, and_7_out, or_1_out);
  and and_9 (and_9_out, ~IR19__16[3], or_2_out);  // AND_Gate
  REG8_LD reg8_ld_7 (.I7__0(MDR), .LD(CREGBUS[8]), .CLK(CLK), .A7__0(DW15__0[7:0]));  // open: mr
  and and_10 (and_10_out, ~IR31__24[3], addrinst);  // AND_Gate
  DC3_8 dc3_8_3 (
    .En(and_10_out), .X2__0(IR31__24[2:0]), .D0(INSTRUCBUS[16]), .D1(INSTRUCBUS[17]), .D2(INSTRUCBUS[18]),
    .D3(INSTRUCBUS[19]), .D4(INSTRUCBUS[20]), .D5(INSTRUCBUS[21]), .D6(INSTRUCBUS[22]), .D7(dc3_8_3_d7));
  and and_11 (and_11_out, ~IR31__24[3], bezaddrinst);  // AND_Gate
  DC3_8 dc3_8_4 (
    .En(and_11_out), .X2__0(IR31__24[2:0]), .D0(INSTRUCBUS[0]), .D1(INSTRUCBUS[1]), .D2(INSTRUCBUS[2]),
    .D3(INSTRUCBUS[3]), .D4(INSTRUCBUS[4]), .D5(INSTRUCBUS[5]), .D6(INSTRUCBUS[6]), .D7(INSTRUCBUS[7]));
  or or_3 (memcheck, and_8_out, pcrel, and_9_out);
  // Probe on PC15__0
  // Probe on BR
  REG16 reg16_2 (
    .LD(RST), .A(16'h8000), .DEC(CMEMBUS[13]), .INC(CMEMBUS[12]), .CLK(CLK), .I(SP15__0));  // open: CL, SL, IL, SR, IR, Cout, Eout, mr
  // Probe on SP15__0
  not not_2 (not_2_out, RST);
  RSFF rsff_1 (.S(CFFBUS[0]), .CLK(CLK), .R(CFFBUS[1]), .Sd(not_2_out), .Q(PHASEFFBUS[0]));  // open: Rd, notQ
  MP4_16b mp4_16b_3 (
    .S0(CMEMBUS[14]), .S1(CMEMBUS[15]), .I0(MAR), .I1({IR23__16, IR19__16, IR15__8}), .I2(ADDJMPREL15__0),
    .I3(DW15__0), .Y(mp4_16b_3_y));  // open: En
  MP2_16b mp2_16b_1 (.En(1'b1), .in_2(mp4_16b_3_y), .in_3(16'h2000), .S0(RST), .out_5(mp2_16b_1_out_5));
  REG16_INC_LD reg16_inc_ld_1 (
    .I15__0(mp2_16b_1_out_5), .LD(or_4_out), .INC(CMEMBUS[4]), .CLK(CLK), .A15__0(PC15__0));  // open: mr
  not not_3 (not_3_out, RST);
  REG2m_INC_DEC_LD reg2m_inc_dec_ld_1 (
    .Ein(CREGBUS[17]), .DEC(CREGBUS[17]), .Cin(CREGBUS[16]), .INC(CREGBUS[16]), .mr(not_3_out), .CLK(CLK),
    .A1__0(BR));  // open: I1__0, LD, Eout, Cout
  or or_4 (or_4_out, CMEMBUS[3], RST);
  RSFF rsff_2 (.S(CFFBUS[2]), .CLK(CLK), .R(CFFBUS[3]), .Rd(not_4_out), .Q(PHASEFFBUS[1]));  // open: Sd, notQ
  not not_4 (not_4_out, RST);
  and and_12 (and_12_out, INSTRUCBUS[3], A[15]);
  and and_13 (and_13_out, INSTRUCBUS[18], C16);
  and and_14 (and_14_out, ~ALU[15], B[15], A[15]);  // AND_Gate
  or or_5 (or_5_out, and_14_out, and_15_out);
  and and_15 (and_15_out, ALU[15], ~B[15], ~A[15]);  // AND_Gate
  // Probe on IVTP15__0
  RSFF rsff_3 (.S(CFFBUS[4]), .CLK(CLK), .R(CFFBUS[5]), .Rd(not_5_out), .Q(PHASEFFBUS[2]));  // open: Sd, notQ
  not not_5 (not_5_out, RST);
  and and_16 (and_16_out, MDR[1], INSTRUCBUS[2]);
  and and_17 (and_17_out, UPDATE, and_18_out);
  and and_18 (and_18_out, ~A[0], ~A[1], ~A[2], ~A[3], ~A[4], ~A[5], ~A[6], ~A[7], ~A[8], ~A[9], ~A[10], ~A[11], ~A[12], ~A[13], ~A[14], ~A[15]);  // AND_Gate
  and and_19 (and_19_out, MDR[3], INSTRUCBUS[2]);
  or or_6 (or_6_out, and_12_out, and_13_out);
  and and_20 (and_20_out, MDR[4], INSTRUCBUS[2]);
  and and_21 (and_21_out, INSTRUCBUS[18], or_5_out);
  or or_7 (or_7_out, and_21_out, and_22_out);
  and and_22 (and_22_out, INSTRUCBUS[7], ALU[15]);
  and and_23 (and_23_out, MDR[7], INSTRUCBUS[2]);
  Multiplexer #(.width(3), .enable("false")) multiplexer_2 (
    .in0(IR19__16[2:0]), .in1({1'b0, BR}), .out(multiplexer_2_out), .sel(CREGBUS[10]));
  MP2_16b mp2_16b_2 (.in_2(A), .in_3(16'hf000), .S0(RST), .out_5(mp2_16b_2_out_5));  // open: En
  REG16 reg16_3 (
    .LD(or_13_out), .A(mp2_16b_2_out_5), .CLK(CLK), .I(IVTP15__0));  // open: CL, SL, IL, SR, IR, DEC, INC, Cout, Eout, mr
  and and_24 (and_24_out, ~MDR[0], INSTRUCBUS[2], CPSW[6]);  // AND_Gate
  or or_8 (or_8_out, and_24_out, CPSW[0]);
  and and_25 (and_25_out, MDR[0], INSTRUCBUS[2], CPSW[6]);
  or or_9 (or_9_out, and_16_out, and_17_out);
  and and_26 (and_26_out, MDR[2], INSTRUCBUS[2]);
  or or_10 (or_10_out, and_26_out, and_27_out);
  and and_27 (and_27_out, UPDATE, A[15]);
  or or_11 (or_11_out, and_19_out, or_6_out);
  or or_12 (or_12_out, and_20_out, or_7_out);
  MP2_16b mp2_16b_3 (.in_2(A), .in_3(DW15__0), .S0(CREGBUS[10]), .out_5(mp2_16b_3_out_5));  // open: En
  // GPR8x16 gpr8x16_1: pin names not known; wires that end beside it: multiplexer_2_out, CLK, mp2_16b_3_out_5, {GPR15__0, GPR7__0}, CREGBUS[3]
  or or_13 (or_13_out, RST, CREGBUS[11]);
  not not_6 (not_6_out, RST);
  RSFF rsff_4 (.S(and_25_out), .CLK(CLK), .R(or_8_out), .Sd(not_6_out), .Q(PSW[0]));  // open: Rd, notQ
  and and_28 (and_28_out, ~or_9_out, CPSW[5]);  // AND_Gate
  and and_29 (and_29_out, or_9_out, CPSW[5]);
  and and_30 (and_30_out, ~or_11_out, CPSW[2]);  // AND_Gate
  and and_31 (and_31_out, or_11_out, CPSW[2]);
  and and_32 (and_32_out, ~and_23_out, CPSW[1]);  // AND_Gate
  and and_33 (and_33_out, and_23_out, CPSW[1]);
  // Probe on {GPR15__0, GPR7__0}
  RSFF rsff_5 (.S(CFFBUS[6]), .CLK(CLK), .R(CFFBUS[7]), .Rd(not_7_out), .Q(PHASEFFBUS[3]));  // open: Sd, notQ
  not not_7 (not_7_out, RST);
  or or_14 (UPDATE, INSTRUCBUS[16], INSTRUCBUS[3], INSTRUCBUS[18], INSTRUCBUS[19], INSTRUCBUS[20], INSTRUCBUS[6], INSTRUCBUS[22], INSTRUCBUS[7]);
  RSFF rsff_6 (.S(and_29_out), .CLK(CLK), .R(and_28_out), .Rd(not_8_out), .Q(PSW[1]));  // open: Sd, notQ
  not not_8 (not_8_out, RST);
  and and_34 (and_34_out, ~or_10_out, CPSW[4]);  // AND_Gate
  and and_35 (and_35_out, or_10_out, CPSW[4]);
  RSFF rsff_7 (.S(and_31_out), .CLK(CLK), .R(and_30_out), .Rd(not_9_out), .Q(PSW[3]));  // open: Sd, notQ
  not not_9 (not_9_out, RST);
  and and_36 (and_36_out, ~or_12_out, CPSW[3]);  // AND_Gate
  RSFF rsff_8 (.S(and_37_out), .CLK(CLK), .R(and_36_out), .Rd(not_10_out), .Q(PSW[4]));  // open: Sd, notQ
  and and_37 (and_37_out, or_12_out, CPSW[3]);
  not not_10 (not_10_out, RST);
  RSFF rsff_9 (.S(and_33_out), .CLK(CLK), .R(and_32_out), .Rd(not_11_out), .Q(PSW[15]));  // open: Sd, notQ
  not not_11 (not_11_out, RST);
  RSFF rsff_10 (.S(and_35_out), .CLK(CLK), .R(and_34_out), .Rd(not_12_out), .Q(PSW[2]));  // open: Sd, notQ
  not not_12 (not_12_out, RST);
  and and_38 (ADDRBUS[0], immed, memcheck);
  and and_39 (ADDRBUS[1], memdir, memcheck);
  and and_40 (ADDRBUS[2], regdir, memcheck);
  and and_41 (ADDRBUS[3], regind, memcheck);
  and and_42 (ADDRBUS[4], pcrel, memcheck);

  assign PSW[14:5] = {10{1'b0}};

  // Other names for the same wires on the sheet: IR23__16[3:0] = IR19__16; BR1__0[1:0] = BR; DWL[7:0] = DW15__0[7:0];
  //   DWH[7:0] = DW15__0[15:8]; A15__0[15:0] = A; ALU15__0[15:0] = ALU; B15__0[15:0] = B; stFETCH = CFFBUS[0];
  //   clFETCH = CFFBUS[1]; stADDR = CFFBUS[2]; clADDR = CFFBUS[3]; stEXEC = CFFBUS[4]; clEXEC = CFFBUS[5];
  //   stINTR = CFFBUS[6]; clINTR = CFFBUS[7]; ldMAR = CMEMBUS[0]; incMAR = CMEMBUS[1]; ldMDR = CMEMBUS[2];
  //   ldPC = CMEMBUS[3]; incPC = CMEMBUS[4]; mxMAR0 = CMEMBUS[5]; mxMAR1 = CMEMBUS[6]; mxMAR2 = CMEMBUS[7];
  //   decMAR = CMEMBUS[8]; mxMDR0 = CMEMBUS[9]; mxMDR1 = CMEMBUS[10]; mxMDR2 = CMEMBUS[11]; incSP = CMEMBUS[12];
  //   decSP = CMEMBUS[13]; mxPC0 = CMEMBUS[14]; mxPC1 = CMEMBUS[15]; mxMDR3 = CMEMBUS[16]; clPSWSTART = CPSW[0];
  //   ldI = CPSW[1]; ldC = CPSW[2]; ldV = CPSW[3]; ldN = CPSW[4]; ldZ = CPSW[5]; ldSTART = CPSW[6]; ldB = CREGBUS[0];
  //   mxB0 = CREGBUS[1]; mxB1 = CREGBUS[2]; wrGPR = CREGBUS[3]; ldIR7__0 = CREGBUS[4]; ldIR15__8 = CREGBUS[5];
  //   ldIR23__16 = CREGBUS[6]; ldIR31__24 = CREGBUS[7]; ldDWL = CREGBUS[8]; ldDWH = CREGBUS[9]; mxGPR = CREGBUS[10];
  //   ldIVTP = CREGBUS[11]; ldA = CREGBUS[12]; slA = CREGBUS[13]; mxA0 = CREGBUS[14]; mxA1 = CREGBUS[15];
  //   incBR = CREGBUS[16]; decBR = CREGBUS[17]; Din7__0[7:0] = DIN; ENTRADDR15__0[15:0] = IVTPPDSP;
  //   GPR15__0[7:0] = GPR7__0; GPR15__8[7:0] = GPR15__0; HALT = INSTRUCBUS[0]; RTS = INSTRUCBUS[1];
  //   RTI = INSTRUCBUS[2]; ASL = INSTRUCBUS[3]; STIVTP = INSTRUCBUS[4]; PUSH = INSTRUCBUS[5]; POP = INSTRUCBUS[6];
  //   ABS = INSTRUCBUS[7]; BEQL = INSTRUCBUS[8]; BNEG = INSTRUCBUS[9]; BGRT = INSTRUCBUS[10]; BGREU = INSTRUCBUS[11];
  //   JLEQ = INSTRUCBUS[12]; BR_t = INSTRUCBUS[13]; JMP = INSTRUCBUS[14]; JSR = INSTRUCBUS[15]; LD = INSTRUCBUS[16];
  //   ST = INSTRUCBUS[17]; ADD = INSTRUCBUS[18]; AND = INSTRUCBUS[19]; SWAP = INSTRUCBUS[20]; JADR = INSTRUCBUS[21];
  //   OR = INSTRUCBUS[22]; MAR15__0[15:0] = MAR; MDR7__0[7:0] = MDR; FETCH = PHASEFFBUS[0]; ADDR = PHASEFFBUS[1];
  //   EXEC = PHASEFFBUS[2]; INTR = PHASEFFBUS[3]; PSW15__0 (some bits) = {PSW[15], PSW[4:0]}; PSWSTART = PSW[0];
  //   PSWZ = PSW[1]; PSWN = PSW[2]; PSWC = PSW[3]; PSWV = PSW[4]; PSWI = PSW[15]

  // Notes on the sheet:
  //   Sabirac
  //   MAR
  //   Instrukcijski registar
  //   Pomocni registri
  //   Akumulator
  //   Dekoderi za prepoznavanje nacina adresiranja
  //   Dekoderi za prepoznavanje instrukcije na osnovu sadrzaja registra IR23..16
  //   MDR
  //   PC
  //   SP
  //   FF za pokretanje FETCH, ADDR, EXEC i INTR faze izvršavanja instrukcije
  //   Registarski fajl
  //   IVTP
  //   Programska statusna reč (PSW)
endmodule

module FETCH (
  input  in_1,
  input  in_2,
  input  in_3,
  input  [3:0] PHASEFFBUS,
  input  [22:0] INSTRUCBUS,
  input  [4:0] ADDRBUS,
  input  [15:0] PSW,
  output [23:0] CMEMBUS,
  output [7:0] CFFBUS,
  output [23:0] CREGBUS,
  output rdMEM
);

  wire addr2, addr_t, and_2_out, and_3_out, and_4_out, and_5_out, and_6_out, and_7_out, and_8_out, and_9_out,
       and_10_out, and_11_out, and_12_out, and_13_out, bezadr1, bradr2, brbezadr1, brcnd, brgraddr, brgrinst,
       brjmp2, brjmp3, brnotfcmem, bruncnd, clFETCH, graddr, grinst, incPC, jmp2, jmp3, ldIR7__0, ldIR15__8,
       ldIR23__16, ldIR31__24, ldMAR, ldMDR, nor_1_out, not_1_out, not_2_out, not_3_out, not_4_out,
       not_5_out, notPSWSTandFETCH, or_4_out, or_5_out, or_7_out, or_8_out, rdMEM_t, stADDR, stEXEC;
  wire [4:0] reg5_cl_inc_ld_1_a4__0, rom32x24_1_dout;
  wire [23:11] rom32x24_1_dout_2;

  or or_1 (jmp3, INSTRUCBUS[12], INSTRUCBUS[14], INSTRUCBUS[15]);
  // Probe on reg5_cl_inc_ld_1_a4__0
  or or_2 (bezadr1, INSTRUCBUS[0], INSTRUCBUS[1], INSTRUCBUS[2], INSTRUCBUS[3], INSTRUCBUS[4], INSTRUCBUS[5], INSTRUCBUS[6], INSTRUCBUS[7]);
  or or_3 (jmp2, INSTRUCBUS[8], INSTRUCBUS[9], INSTRUCBUS[10], INSTRUCBUS[11], INSTRUCBUS[13]);
  not not_1 (not_1_out, in_1);
  REG5_CL_INC_LD reg5_cl_inc_ld_1 (
    .I4__0(rom32x24_1_dout), .LD(or_4_out), .CL(1'b0), .INC(not_2_out), .CLK(in_2),
    .A4__0(reg5_cl_inc_ld_1_a4__0), .mr(not_1_out));
  not not_2 (not_2_out, or_4_out);
  ROM32X24 rom32x24_1 (
    .A4__0(reg5_cl_inc_ld_1_a4__0), .CS(1'b1),
    .DOUT({rom32x24_1_dout_2[23:21], rom32x24_1_dout, rom32x24_1_dout_2[15:11], stEXEC, stADDR, clFETCH, ldIR7__0, ldIR15__8, ldIR23__16, ldIR31__24, ldMDR, rdMEM_t, incPC, ldMAR}));
  DC4_16 dc4_16_1 (
    .En(1'b1), .X3__0(rom32x24_1_dout_2[15:12]), .D1(bruncnd), .D2(notPSWSTandFETCH), .D3(brbezadr1),
    .D4(brjmp2), .D5(bradr2), .D6(brjmp3), .D7(brnotfcmem), .D8(brgrinst), .D9(brgraddr));  // open: D0, D10, D11, D12, D13, D14, D15
  or or_4 (or_4_out, bruncnd, brcnd);
  or or_5 (or_5_out, ADDRBUS[2], ADDRBUS[3], ADDRBUS[4]);
  or or_6 (addr_t, INSTRUCBUS[16], INSTRUCBUS[17], INSTRUCBUS[18], INSTRUCBUS[19], INSTRUCBUS[20], INSTRUCBUS[21], INSTRUCBUS[22]);
  and and_1 (addr2, addr_t, or_5_out);
  and and_2 (and_2_out, addr_t, nor_1_out);
  nor nor_1 (nor_1_out, ADDRBUS[0], ADDRBUS[1], ADDRBUS[2], ADDRBUS[3], ADDRBUS[4]);
  not not_3 (not_3_out, PHASEFFBUS[0]);
  not not_4 (not_4_out, PSW[0]);
  or or_7 (or_7_out, not_3_out, not_4_out);
  not not_5 (not_5_out, in_3);
  nor nor_2 (grinst, INSTRUCBUS[0], INSTRUCBUS[1], INSTRUCBUS[2], INSTRUCBUS[3], INSTRUCBUS[4], INSTRUCBUS[5], INSTRUCBUS[6], INSTRUCBUS[7], INSTRUCBUS[8], INSTRUCBUS[9], INSTRUCBUS[10], INSTRUCBUS[11], INSTRUCBUS[12], INSTRUCBUS[13], INSTRUCBUS[14], INSTRUCBUS[15], addr_t);
  and and_3 (and_3_out, INSTRUCBUS[17], ADDRBUS[0]);
  and and_4 (and_4_out, ADDRBUS[0], INSTRUCBUS[20]);
  or or_8 (or_8_out, ADDRBUS[0], ADDRBUS[2]);
  and and_5 (and_5_out, brgrinst, grinst);
  and and_6 (and_6_out, or_7_out, notPSWSTandFETCH);
  and and_7 (and_7_out, brbezadr1, bezadr1);
  and and_8 (and_8_out, brjmp2, jmp2);
  and and_9 (and_9_out, bradr2, addr2);
  and and_10 (and_10_out, brjmp3, jmp3);
  and and_11 (and_11_out, brnotfcmem, not_5_out);
  and and_12 (and_12_out, brgraddr, graddr);
  and and_13 (and_13_out, INSTRUCBUS[21], or_8_out);
  or or_9 (graddr, and_3_out, and_4_out, and_2_out, and_13_out);
  or or_10 (brcnd, and_5_out, and_6_out, and_7_out, and_8_out, and_9_out, and_10_out, and_11_out, and_12_out);
  assign CMEMBUS[0] = ldMAR ? 1'b1 : 1'bz;  // Controlled_Buffer controlled_buffer_1
  assign CMEMBUS[2] = ldMDR ? 1'b1 : 1'bz;  // Controlled_Buffer controlled_buffer_2
  assign CMEMBUS[4] = incPC ? 1'b1 : 1'bz;  // Controlled_Buffer controlled_buffer_3
  assign CFFBUS[1] = clFETCH ? 1'b1 : 1'bz;  // Controlled_Buffer controlled_buffer_4
  assign CFFBUS[2] = stADDR ? 1'b1 : 1'bz;  // Controlled_Buffer controlled_buffer_5
  assign CFFBUS[4] = stEXEC ? 1'b1 : 1'bz;  // Controlled_Buffer controlled_buffer_6
  assign CREGBUS[4] = ldIR7__0 ? 1'b1 : 1'bz;  // Controlled_Buffer controlled_buffer_7
  assign CREGBUS[5] = ldIR15__8 ? 1'b1 : 1'bz;  // Controlled_Buffer controlled_buffer_8
  assign CREGBUS[6] = ldIR23__16 ? 1'b1 : 1'bz;  // Controlled_Buffer controlled_buffer_9
  assign CREGBUS[7] = ldIR31__24 ? 1'b1 : 1'bz;  // Controlled_Buffer controlled_buffer_10
  assign rdMEM = rdMEM_t ? 1'b1 : 1'bz;  // Controlled_Buffer controlled_buffer_11

  // Other names for the same wires on the sheet: immed = ADDRBUS[0]; memdir = ADDRBUS[1]; regdir = ADDRBUS[2];
  //   regind = ADDRBUS[3]; pcrel = ADDRBUS[4]; CLK = in_2; FCBUS = in_3; HALT = INSTRUCBUS[0]; RTS = INSTRUCBUS[1];
  //   RTI = INSTRUCBUS[2]; ASL = INSTRUCBUS[3]; STIVTP = INSTRUCBUS[4]; PUSH = INSTRUCBUS[5]; POP = INSTRUCBUS[6];
  //   ABS = INSTRUCBUS[7]; BEQL = INSTRUCBUS[8]; BNEG = INSTRUCBUS[9]; BGRT = INSTRUCBUS[10]; BGREU = INSTRUCBUS[11];
  //   JLEQ = INSTRUCBUS[12]; BR = INSTRUCBUS[13]; JMP = INSTRUCBUS[14]; JSR = INSTRUCBUS[15]; LD = INSTRUCBUS[16];
  //   ST = INSTRUCBUS[17]; ADD = INSTRUCBUS[18]; AND = INSTRUCBUS[19]; SWAP = INSTRUCBUS[20]; JADR = INSTRUCBUS[21];
  //   OR = INSTRUCBUS[22]; FETCH = PHASEFFBUS[0]; ADDR = PHASEFFBUS[1]; EXEC = PHASEFFBUS[2]; INTR = PHASEFFBUS[3];
  //   PSWSTART = PSW[0]; rst = in_1

  // Notes on the sheet:
  //   Operaciona jedinica
  //   Kontrolna jedinica
endmodule

module ADDR (
  input  in_1,
  input  in_2,
  input  in_3,
  input  [3:0] PHASEFFBUS,
  input  [22:0] INSTRUCBUS,
  input  [4:0] ADDRBUS,
  output [23:0] CMEMBUS,
  output [7:0] CFFBUS,
  output [23:0] CREGBUS,
  output rdMEM
);

  wire and_1_out, and_2_out, and_3_out, bradr, brcnd, brnotADDR, brnotfcbus, brSTOREorJADR, bruncnd, clADDR,
       decMAR, incMAR, ldB, ldDWH, ldDWL, ldMAR, ldMDR, mxB0, mxB1, mxMAR0, mxMAR1, not_1_out, not_2_out,
       not_3_out, not_4_out, or_1_out, or_2_out, rdMEM_t, stEXEC;
  wire [3:0] kmadr_1_adr3__0, mp2_4b_1_y, reg4_inc_ld_1_a3__0, rom15x21_1_dout;
  wire [16:14] rom15x21_1_dout_2;

  not not_1 (not_1_out, in_1);
  // Probe on reg4_inc_ld_1_a3__0
  KMADR kmadr_1 (
    .immed(ADDRBUS[0]), .memdir(ADDRBUS[1]), .regdir(ADDRBUS[2]), .regind(ADDRBUS[3]),
    .Adr3__0(kmadr_1_adr3__0), .pcrel(ADDRBUS[4]));
  MP2_4b mp2_4b_1 (.En(1'b1), .in_2(rom15x21_1_dout), .in_3(kmadr_1_adr3__0), .S0(bradr), .Y(mp2_4b_1_y));
  REG4_INC_LD reg4_inc_ld_1 (
    .I3__0(mp2_4b_1_y), .LD(or_1_out), .INC(not_2_out), .mr(not_1_out), .CLK(in_2),
    .A3__0(reg4_inc_ld_1_a3__0));
  not not_2 (not_2_out, or_1_out);
  ROM15X21 rom15x21_1 (
    .A3__0(reg4_inc_ld_1_a3__0), .CS(1'b1),
    .DOUT({rom15x21_1_dout, rom15x21_1_dout_2, stEXEC, clADDR, ldMDR, rdMEM_t, mxMAR1, mxB1, mxMAR0, ldMAR, mxB0, ldB, ldDWH, ldDWL, incMAR, decMAR}));
  DC3_8 dc3_8_1 (
    .En(1'b1), .X2__0(rom15x21_1_dout_2), .D1(bruncnd), .D2(brnotADDR), .D3(brSTOREorJADR), .D4(brnotfcbus),
    .D5(bradr));  // open: D0, D6, D7
  or or_1 (or_1_out, bruncnd, brcnd, bradr);
  not not_3 (not_3_out, PHASEFFBUS[1]);
  or or_2 (or_2_out, INSTRUCBUS[21], INSTRUCBUS[17]);
  not not_4 (not_4_out, in_3);
  and and_1 (and_1_out, not_3_out, brnotADDR);
  and and_2 (and_2_out, or_2_out, brSTOREorJADR);
  and and_3 (and_3_out, brnotfcbus, not_4_out);
  or or_3 (brcnd, and_1_out, and_2_out, and_3_out);
  assign CMEMBUS[0] = ldMAR ? 1'b1 : 1'bz;  // Controlled_Buffer controlled_buffer_1
  assign CMEMBUS[1] = incMAR ? 1'b1 : 1'bz;  // Controlled_Buffer controlled_buffer_2
  assign CMEMBUS[2] = ldMDR ? 1'b1 : 1'bz;  // Controlled_Buffer controlled_buffer_3
  assign CMEMBUS[5] = mxMAR0 ? 1'b1 : 1'bz;  // Controlled_Buffer controlled_buffer_4
  assign CMEMBUS[6] = mxMAR1 ? 1'b1 : 1'bz;  // Controlled_Buffer controlled_buffer_5
  assign CMEMBUS[8] = decMAR ? 1'b1 : 1'bz;  // Controlled_Buffer controlled_buffer_6
  assign CFFBUS[3] = clADDR ? 1'b1 : 1'bz;  // Controlled_Buffer controlled_buffer_7
  assign CFFBUS[4] = stEXEC ? 1'b1 : 1'bz;  // Controlled_Buffer controlled_buffer_8
  assign CREGBUS[0] = ldB ? 1'b1 : 1'bz;  // Controlled_Buffer controlled_buffer_9
  assign CREGBUS[1] = mxB0 ? 1'b1 : 1'bz;  // Controlled_Buffer controlled_buffer_10
  assign CREGBUS[2] = mxB1 ? 1'b1 : 1'bz;  // Controlled_Buffer controlled_buffer_11
  assign CREGBUS[8] = ldDWL ? 1'b1 : 1'bz;  // Controlled_Buffer controlled_buffer_12
  assign CREGBUS[9] = ldDWH ? 1'b1 : 1'bz;  // Controlled_Buffer controlled_buffer_13
  assign rdMEM = rdMEM_t ? 1'b1 : 1'bz;  // Controlled_Buffer controlled_buffer_14

  // Other names for the same wires on the sheet: immed = ADDRBUS[0]; memdir = ADDRBUS[1]; regdir = ADDRBUS[2];
  //   regind = ADDRBUS[3]; pcrel = ADDRBUS[4]; CLK = in_2; FCBUS = in_3; HALT = INSTRUCBUS[0]; RTS = INSTRUCBUS[1];
  //   RTI = INSTRUCBUS[2]; ASL = INSTRUCBUS[3]; STIVTP = INSTRUCBUS[4]; PUSH = INSTRUCBUS[5]; POP = INSTRUCBUS[6];
  //   ABS = INSTRUCBUS[7]; BEQL = INSTRUCBUS[8]; BNEG = INSTRUCBUS[9]; BGRT = INSTRUCBUS[10]; BGREU = INSTRUCBUS[11];
  //   JLEQ = INSTRUCBUS[12]; BR = INSTRUCBUS[13]; JMP = INSTRUCBUS[14]; JSR = INSTRUCBUS[15]; LD = INSTRUCBUS[16];
  //   ST = INSTRUCBUS[17]; ADD = INSTRUCBUS[18]; AND = INSTRUCBUS[19]; SWAP = INSTRUCBUS[20]; JADR = INSTRUCBUS[21];
  //   OR = INSTRUCBUS[22]; ADDR = PHASEFFBUS[1]; rst = in_1

  // Notes on the sheet:
  //   Operaciona jedinica
  //   Upravljacka jedinica
endmodule

module EXEC (
  input  [15:0] A,
  input  in_2,
  input  in_3,
  input  in_4,
  input  [15:0] B,
  input  [3:0] PHASEFFBUS,
  input  [22:0] INSTRUCBUS,
  input  [4:0] ADDRBUS,
  input  [15:0] PSW,
  input  [1:0] DW,
  output [15:0] ALU,
  output [23:0] CMEMBUS,
  output [7:0] CFFBUS,
  output [23:0] CREGBUS,
  output C16,
  output [6:0] CPSW,
  output rdMEM,
  output wrMEM
);

  wire abs_t, add_t, and_1_out, and_2_out, and_3_out, and_4_out, and_5_out, and_6_out, and_7_out, and_8_out,
       and_9_out, and_10_out, and_11_out, and_12_out, and_13_out, and_t, brcnd, brnotBR0, brnotbrorjmp,
       brnotEXEC, brnotFCBUS, brnotregdir, bropr, brorjmp, brPOP, brregdir, brST, bruncnd, clEXEC,
       clPSWSTART, decBR, decSP, incMAR, incSP, ldA, ldC, ldDWH, ldDWL, ldI, ldIVTP, ldMAR, ldMDR, ldN, ldPC,
       ldSTART, ldV, ldZ, mxA0, mxA1, mxGPR, mxMAR2, mxMDR0, mxMDR1, mxMDR2, mxPC0, mxPC1, not_1_out,
       not_2_out, not_3_out, not_4_out, not_5_out, not_6_out, or_1_out, or_2_out, or_3_out, or_4_out,
       or_5_out, or_t, rdMEM_t, slA, stINTR, wrGPR, wrMEM_t, xor_1_out;
  wire [3:0] rom64x47_1_dout46__32;
  wire [5:0] mp2_6b_1_p4, mp2_6b_1_p5, mp2_6b_1_p6, reg6_inc_ld_1_a5__0;

  DC4_16 dc4_16_1 (
    .En(1'b1), .X3__0(rom64x47_1_dout46__32), .D1(bruncnd), .D2(brnotEXEC), .D3(brST), .D4(brregdir),
    .D5(brnotbrorjmp), .D6(brnotFCBUS), .D7(brPOP), .D8(brnotBR0), .D9(brnotregdir), .D10(bropr));  // open: D0, D11, D12, D13, D14, D15
  or or_1 (or_1_out, INSTRUCBUS[8], INSTRUCBUS[9], INSTRUCBUS[10], INSTRUCBUS[11]);
  not not_1 (not_1_out, in_2);
  // Probe on reg6_inc_ld_1_a5__0
  // MP2_6b mp2_6b_1: pin names not known; wires that end beside it: INSTRUCBUS[17], INSTRUCBUS[19], bropr, mp2_6b_1_p4, mp2_6b_1_p5, mp2_6b_1_p6, 1'b1
  REG6_INC_LD reg6_inc_ld_1 (
    .I5__0(mp2_6b_1_p5), .LD(or_2_out), .INC(not_2_out), .mr(not_1_out), .CLK(in_3),
    .A5__0(reg6_inc_ld_1_a5__0));
  not not_2 (not_2_out, or_2_out);
  ROM64X47 rom64x47_1 (
    .A5__0(reg6_inc_ld_1_a5__0), .CS(1'b1),
    .DOUT46__32({mp2_6b_1_p4, rom64x47_1_dout46__32, clEXEC, stINTR, clPSWSTART, ldSTART, ldI}),
    .DOUT31__0({mxPC1, ldDWH, ldDWL, rdMEM_t, incSP, mxMDR2, decSP, ldMAR, mxMAR2, mxMDR1, ldPC, mxPC0, and_t, ldV, add_t, mxA0, wrGPR, wrMEM_t, ldMDR, mxMDR0, ldZ, ldN, ldA, ldC, or_t, mxA1, slA, ldIVTP, abs_t, decBR, incMAR, mxGPR}));
  KMOPR kmopr_1 (
    .LD(INSTRUCBUS[16]), .ST(INSTRUCBUS[17]), .ADD(INSTRUCBUS[18]), .SWAP(INSTRUCBUS[20]), .BX(or_1_out),
    .BR(INSTRUCBUS[13]), .JLEQ(INSTRUCBUS[12]), .JMP(INSTRUCBUS[14]), .JSR(INSTRUCBUS[15]),
    .POP_RTS(or_3_out), .ASL(INSTRUCBUS[3]), .Adr5__0(mp2_6b_1_p6), .STIVTP(INSTRUCBUS[4]),
    .PUSH(INSTRUCBUS[5]), .ABS(INSTRUCBUS[7]), .RTI(INSTRUCBUS[2]), .AND(INSTRUCBUS[19]),
    .JADR(INSTRUCBUS[21]), .OR(INSTRUCBUS[22]), .HALT(INSTRUCBUS[0]));
  or or_2 (or_2_out, bruncnd, brcnd, bropr);
  ALU16b alu16b_1 (
    .Cin(1'b0), .A(A), .B(B), .add(add_t), .\and (and_t), .sub(1'b0), .\or (or_t), .abs(abs_t), .F(ALU),
    .Cout(C16));
  or or_3 (or_3_out, INSTRUCBUS[1], INSTRUCBUS[6]);
  xor xor_1 (xor_1_out, PSW[2], PSW[4]);
  or or_4 (or_4_out, xor_1_out, PSW[1]);
  not not_3 (not_3_out, PHASEFFBUS[2]);
  not not_4 (not_4_out, brorjmp);
  not not_5 (not_5_out, in_4);
  or or_5 (or_5_out, DW[0], DW[1]);
  not not_6 (not_6_out, ADDRBUS[2]);
  and and_1 (and_1_out, ~PSW[3], INSTRUCBUS[11]);  // AND_Gate
  and and_2 (and_2_out, PSW[2], INSTRUCBUS[9]);
  and and_3 (and_3_out, ~or_4_out, INSTRUCBUS[10]);  // AND_Gate
  and and_4 (and_4_out, or_4_out, INSTRUCBUS[12]);
  and and_5 (and_5_out, PSW[1], INSTRUCBUS[8]);
  and and_6 (and_6_out, not_3_out, brnotEXEC);
  and and_7 (and_7_out, INSTRUCBUS[17], brST);
  and and_8 (and_8_out, ADDRBUS[2], brregdir);
  and and_9 (and_9_out, not_4_out, brnotbrorjmp);
  and and_10 (and_10_out, not_5_out, brnotFCBUS);
  and and_11 (and_11_out, INSTRUCBUS[6], brPOP);
  and and_12 (and_12_out, or_5_out, brnotBR0);
  and and_13 (and_13_out, not_6_out, brnotregdir);
  or or_6 (brorjmp, and_1_out, and_2_out, and_3_out, and_4_out, and_5_out);
  or or_7 (brcnd, and_6_out, and_7_out, and_8_out, and_9_out, and_10_out, and_11_out, and_12_out, and_13_out);
  assign CMEMBUS[0] = ldMAR ? 1'b1 : 1'bz;  // Controlled_Buffer controlled_buffer_1
  assign CMEMBUS[1] = incMAR ? 1'b1 : 1'bz;  // Controlled_Buffer controlled_buffer_2
  assign CMEMBUS[2] = ldMDR ? 1'b1 : 1'bz;  // Controlled_Buffer controlled_buffer_3
  assign CMEMBUS[3] = ldPC ? 1'b1 : 1'bz;  // Controlled_Buffer controlled_buffer_4
  assign CMEMBUS[7] = mxMAR2 ? 1'b1 : 1'bz;  // Controlled_Buffer controlled_buffer_5
  assign CMEMBUS[9] = mxMDR0 ? 1'b1 : 1'bz;  // Controlled_Buffer controlled_buffer_6
  assign CMEMBUS[10] = mxMDR1 ? 1'b1 : 1'bz;  // Controlled_Buffer controlled_buffer_7
  assign CMEMBUS[11] = mxMDR2 ? 1'b1 : 1'bz;  // Controlled_Buffer controlled_buffer_8
  assign CMEMBUS[12] = incSP ? 1'b1 : 1'bz;  // Controlled_Buffer controlled_buffer_9
  assign CMEMBUS[13] = decSP ? 1'b1 : 1'bz;  // Controlled_Buffer controlled_buffer_10
  assign CMEMBUS[14] = mxPC0 ? 1'b1 : 1'bz;  // Controlled_Buffer controlled_buffer_11
  assign CMEMBUS[15] = mxPC1 ? 1'b1 : 1'bz;  // Controlled_Buffer controlled_buffer_12
  assign CFFBUS[5] = clEXEC ? 1'b1 : 1'bz;  // Controlled_Buffer controlled_buffer_13
  assign CFFBUS[6] = stINTR ? 1'b1 : 1'bz;  // Controlled_Buffer controlled_buffer_14
  assign CREGBUS[3] = wrGPR ? 1'b1 : 1'bz;  // Controlled_Buffer controlled_buffer_15
  assign CREGBUS[8] = ldDWL ? 1'b1 : 1'bz;  // Controlled_Buffer controlled_buffer_16
  assign CREGBUS[9] = ldDWH ? 1'b1 : 1'bz;  // Controlled_Buffer controlled_buffer_17
  assign CREGBUS[10] = mxGPR ? 1'b1 : 1'bz;  // Controlled_Buffer controlled_buffer_18
  assign CREGBUS[11] = ldIVTP ? 1'b1 : 1'bz;  // Controlled_Buffer controlled_buffer_19
  assign CREGBUS[12] = ldA ? 1'b1 : 1'bz;  // Controlled_Buffer controlled_buffer_20
  assign CREGBUS[13] = slA ? 1'b1 : 1'bz;  // Controlled_Buffer controlled_buffer_21
  assign CREGBUS[14] = mxA0 ? 1'b1 : 1'bz;  // Controlled_Buffer controlled_buffer_22
  assign CREGBUS[15] = mxA1 ? 1'b1 : 1'bz;  // Controlled_Buffer controlled_buffer_23
  assign CREGBUS[17] = decBR ? 1'b1 : 1'bz;  // Controlled_Buffer controlled_buffer_24
  assign CPSW[0] = clPSWSTART ? 1'b1 : 1'bz;  // Controlled_Buffer controlled_buffer_25
  assign CPSW[1] = ldI ? 1'b1 : 1'bz;  // Controlled_Buffer controlled_buffer_26
  assign CPSW[2] = ldC ? 1'b1 : 1'bz;  // Controlled_Buffer controlled_buffer_27
  assign CPSW[3] = ldV ? 1'b1 : 1'bz;  // Controlled_Buffer controlled_buffer_28
  assign CPSW[4] = ldN ? 1'b1 : 1'bz;  // Controlled_Buffer controlled_buffer_29
  assign CPSW[5] = ldZ ? 1'b1 : 1'bz;  // Controlled_Buffer controlled_buffer_30
  assign CPSW[6] = ldSTART ? 1'b1 : 1'bz;  // Controlled_Buffer controlled_buffer_31
  assign rdMEM = rdMEM_t ? 1'b1 : 1'bz;  // Controlled_Buffer controlled_buffer_32
  assign wrMEM = wrMEM_t ? 1'b1 : 1'bz;  // Controlled_Buffer controlled_buffer_33

  // Other names for the same wires on the sheet: A15__0[15:0] = A; immed = ADDRBUS[0]; regdir = ADDRBUS[2];
  //   ALU15__0[15:0] = ALU; B15__0[15:0] = B; BR1__0[1:0] = DW; CLK = in_3; FCBUS = in_4; HALT = INSTRUCBUS[0];
  //   RTS = INSTRUCBUS[1]; RTI = INSTRUCBUS[2]; ASL = INSTRUCBUS[3]; STIVTP = INSTRUCBUS[4]; PUSH = INSTRUCBUS[5];
  //   POP = INSTRUCBUS[6]; ABS = INSTRUCBUS[7]; BEQL = INSTRUCBUS[8]; BNEG = INSTRUCBUS[9]; BGRT = INSTRUCBUS[10];
  //   BGREU = INSTRUCBUS[11]; JLEQ = INSTRUCBUS[12]; BR = INSTRUCBUS[13]; JMP = INSTRUCBUS[14]; JSR = INSTRUCBUS[15];
  //   LD = INSTRUCBUS[16]; ST = INSTRUCBUS[17]; ADD = INSTRUCBUS[18]; AND = INSTRUCBUS[19]; SWAP = INSTRUCBUS[20];
  //   JADR = INSTRUCBUS[21]; OR = INSTRUCBUS[22]; EXEC = PHASEFFBUS[2]; PSWSTART = PSW[0]; PSWZ = PSW[1];
  //   PSWN = PSW[2]; PSWC = PSW[3]; PSWV = PSW[4]; PSWI = PSW[15]; rst = in_2

  // Notes on the sheet:
  //   Operaciona jedinica
  //   Upravljacka jedinica
  //   ALU
  //   Uslov za skok
endmodule

module INTR (
  input  in_1,
  input  in_2,
  input  in_3,
  input  [3:0] PHASEFFBUS,
  input  [22:0] INSTRUCBUS,
  input  [15:0] PSW,
  input  [3:0] intr,
  input  [15:0] IVTP,
  input  [1:0] DW,
  output [15:0] ADDIVTP,
  output [1:0] UEXT1__0,
  output inta,
  output [23:0] CMEMBUS,
  output [7:0] CFFBUS,
  output [23:0] CREGBUS,
  output rdMEM,
  output wrMEM
);

  wire and_2_out, and_3_out, and_4_out, and_5_out, brcnd, brnotBR3, brnotFCBUS, brnotINTR, brnotprekid,
       bruncnd, clINTR, decSP, incBR, incMAR, incSP, ldDWH, ldDWL, ldMAR, ldMDR, ldPC, mxGPR, mxMAR0, mxMAR2,
       mxMDR0, mxMDR1, mxMDR2, mxMDR3, mxPC0, mxPC1, nand_1_out, not_1_out, not_2_out, not_3_out, not_4_out,
       not_5_out, not_6_out, or_2_out, prekid, prper, rdMEM_t, stFETCH, wrMEM_t;
  wire [2:0] rom32x31_1_dout_2;
  wire [2:1] IVTDSP15__0;
  wire [4:0] reg5_cl_inc_ld_1_a4__0, rom32x31_1_dout;

  and and_1 (prekid, prper, 1'b1, not_2_out);
  not not_1 (not_1_out, in_1);
  REG5_CL_INC_LD reg5_cl_inc_ld_1 (
    .I4__0(rom32x31_1_dout), .LD(or_2_out), .INC(not_3_out), .CLK(in_2), .A4__0(reg5_cl_inc_ld_1_a4__0),
    .mr(not_1_out));  // open: CL
  // Probe on reg5_cl_inc_ld_1_a4__0
  DC3_8 dc3_8_1 (
    .En(1'b1), .X2__0(rom32x31_1_dout_2), .D1(bruncnd), .D2(brnotINTR), .D3(brnotprekid), .D4(brnotFCBUS),
    .D5(brnotBR3));  // open: D0, D6, D7
  not not_2 (not_2_out, INSTRUCBUS[0]);
  not not_3 (not_3_out, or_2_out);
  ROM32X31 rom32x31_1 (
    .A4__0(reg5_cl_inc_ld_1_a4__0), .CS(1'b1),
    .DOUT({rom32x31_1_dout, rom32x31_1_dout_2, clINTR, stFETCH, mxPC1, ldPC, ldDWH, ldDWL, incMAR, rdMEM_t, mxMAR2, inta, mxMDR2, mxMDR0, wrMEM_t, ldMDR, mxMDR1, decSP, ldMAR, mxMDR3, mxMAR0, incSP, mxPC0, mxGPR, incBR}));
  or or_1 (prper, intr[0], intr[1], intr[2], intr[3]);
  or or_2 (or_2_out, bruncnd, brcnd);
  Priority_Encoder #(.select(2)) priority_encoder_1 (
    .in0(intr[0]), .in1(intr[1]), .in2(intr[2]), .in3(intr[3]), .out(UEXT1__0), .en_in(1'b1));  // open: gs, en_out
  REG2_LD reg2_ld_1 (.LD(inta), .CLK(in_2), .I1__0(UEXT1__0), .A1__0(IVTDSP15__0));  // open: mr
  ADD16 add16_1 (.C0(1'b0), .A(IVTP), .B({{13{1'b0}}, IVTDSP15__0, 1'b0}), .F(ADDIVTP));  // open: C16
  not not_4 (not_4_out, PHASEFFBUS[3]);
  not not_5 (not_5_out, prekid);
  not not_6 (not_6_out, in_3);
  nand nand_1 (nand_1_out, DW[0], DW[1]);
  and and_2 (and_2_out, not_4_out, brnotINTR);
  and and_3 (and_3_out, not_5_out, brnotprekid);
  and and_4 (and_4_out, not_6_out, brnotFCBUS);
  and and_5 (and_5_out, nand_1_out, brnotBR3);
  or or_3 (brcnd, and_2_out, and_3_out, and_4_out, and_5_out);
  assign CMEMBUS[0] = ldMAR ? 1'b1 : 1'bz;  // Controlled_Buffer controlled_buffer_1
  assign CMEMBUS[1] = incMAR ? 1'b1 : 1'bz;  // Controlled_Buffer controlled_buffer_2
  assign CMEMBUS[2] = ldMDR ? 1'b1 : 1'bz;  // Controlled_Buffer controlled_buffer_3
  assign CMEMBUS[3] = ldPC ? 1'b1 : 1'bz;  // Controlled_Buffer controlled_buffer_4
  assign CMEMBUS[5] = mxMAR0 ? 1'b1 : 1'bz;  // Controlled_Buffer controlled_buffer_5
  assign CMEMBUS[7] = mxMAR2 ? 1'b1 : 1'bz;  // Controlled_Buffer controlled_buffer_6
  assign CMEMBUS[9] = mxMDR0 ? 1'b1 : 1'bz;  // Controlled_Buffer controlled_buffer_7
  assign CMEMBUS[10] = mxMDR1 ? 1'b1 : 1'bz;  // Controlled_Buffer controlled_buffer_8
  assign CMEMBUS[11] = mxMDR2 ? 1'b1 : 1'bz;  // Controlled_Buffer controlled_buffer_9
  assign CMEMBUS[12] = incSP ? 1'b1 : 1'bz;  // Controlled_Buffer controlled_buffer_10
  assign CMEMBUS[13] = decSP ? 1'b1 : 1'bz;  // Controlled_Buffer controlled_buffer_11
  assign CMEMBUS[14] = mxPC0 ? 1'b1 : 1'bz;  // Controlled_Buffer controlled_buffer_12
  assign CMEMBUS[15] = mxPC1 ? 1'b1 : 1'bz;  // Controlled_Buffer controlled_buffer_13
  assign CMEMBUS[16] = mxMDR3 ? 1'b1 : 1'bz;  // Controlled_Buffer controlled_buffer_14
  assign CFFBUS[0] = stFETCH ? 1'b1 : 1'bz;  // Controlled_Buffer controlled_buffer_15
  assign CFFBUS[7] = clINTR ? 1'b1 : 1'bz;  // Controlled_Buffer controlled_buffer_16
  assign CREGBUS[8] = ldDWL ? 1'b1 : 1'bz;  // Controlled_Buffer controlled_buffer_17
  assign CREGBUS[9] = ldDWH ? 1'b1 : 1'bz;  // Controlled_Buffer controlled_buffer_18
  assign CREGBUS[10] = mxGPR ? 1'b1 : 1'bz;  // Controlled_Buffer controlled_buffer_19
  assign CREGBUS[16] = incBR ? 1'b1 : 1'bz;  // Controlled_Buffer controlled_buffer_20
  assign rdMEM = rdMEM_t ? 1'b1 : 1'bz;  // Controlled_Buffer controlled_buffer_21
  assign wrMEM = wrMEM_t ? 1'b1 : 1'bz;  // Controlled_Buffer controlled_buffer_22

  // Other names for the same wires on the sheet: ldBRU = inta; ADDIVTP15__0[15:0] = ADDIVTP; BR1__0[1:0] = DW;
  //   CLK = in_2; FCBUS = in_3; HALT = INSTRUCBUS[0]; RTS = INSTRUCBUS[1]; RTI = INSTRUCBUS[2]; ASL = INSTRUCBUS[3];
  //   STIVTP = INSTRUCBUS[4]; PUSH = INSTRUCBUS[5]; POP = INSTRUCBUS[6]; ABS = INSTRUCBUS[7]; BEQL = INSTRUCBUS[8];
  //   BNEG = INSTRUCBUS[9]; BGRT = INSTRUCBUS[10]; BGREU = INSTRUCBUS[11]; JLEQ = INSTRUCBUS[12]; BR = INSTRUCBUS[13];
  //   JMP = INSTRUCBUS[14]; JSR = INSTRUCBUS[15]; LD = INSTRUCBUS[16]; ST = INSTRUCBUS[17]; ADD = INSTRUCBUS[18];
  //   AND = INSTRUCBUS[19]; SWAP = INSTRUCBUS[20]; JADR = INSTRUCBUS[21]; OR = INSTRUCBUS[22]; intr3__0[3:0] = intr;
  //   IVTP15__0[15:0] = IVTP; INTR_t = PHASEFFBUS[3]; PSWI = PSW[15]; rst = in_1

  // Notes on the sheet:
  //   Operaciona jedinica
  //   Upravljacka jedinica
endmodule

module RAM (
  input  [15:0] in_1,
  input  in_2,
  input  [7:0] in_3,
  input  in_4,
  input  in_5,
  input  in_6,
  output [7:0] out_7,
  output out_8
);

  wire and_1_out, and_2_out, CNT0, LDCNT, not_1_out, not_2_out, not_3_out, notCNT0, or_1_out, rsff_2_q, sl,
       xor_1_out;
  wire [3:0] CNT, LFSR;

  RSFF rsff_1 (.S(in_6), .CLK(in_2), .R(1'b0), .Q(sl));  // open: Sd, Rd, notQ
  or or_1 (or_1_out, in_4, in_5);
  REG4_LD_SL_SR reg4_ld_sl_sr_1 (
    .I3__0(4'b1111), .LD(in_6), .IR(1'b0), .SR(1'b0), .IL(xor_1_out), .SL(sl), .CLK(in_2), .A3__0(LFSR));  // open: mr
  RisingEdge risingedge_1 (.INPUT(or_1_out), .CLK(in_2), .OUTPUT(LDCNT));
  MEM64Kx8 mem64kx8_1 (.WR_RD(in_4), .A15__0(in_1), .DIN(in_3), .CS(1'b1), .CLK(in_2), .DOUT(out_7));
  xor xor_1 (xor_1_out, LFSR[2], LFSR[3]);
  and and_1 (and_1_out, CNT0, not_1_out);
  not not_1 (not_1_out, LDCNT);
  RSFF rsff_2 (.S(LDCNT), .CLK(in_2), .R(and_1_out), .Rd(not_2_out), .Q(rsff_2_q));  // open: Sd, notQ
  not not_2 (not_2_out, in_6);
  and and_2 (and_2_out, rsff_2_q, CNT0);
  REG4m_DEC_LD reg4m_dec_ld_1 (
    .I3__0(LFSR), .LD(LDCNT), .Ein(notCNT0), .DEC(notCNT0), .CLK(in_2), .A3__0(CNT));  // open: Eout, mr
  or or_2 (notCNT0, CNT[0], CNT[1], CNT[2], CNT[3]);
  RSFF rsff_3 (.S(and_2_out), .CLK(in_2), .R(out_8), .Rd(not_3_out), .Q(out_8));  // open: Sd, notQ
  not not_3 (not_3_out, in_6);
  not not_4 (CNT0, notCNT0);

  // Other names for the same wires on the sheet: ADR[15:0] = in_1; CLK = in_2; DIN[7:0] = in_3; DOUT[7:0] = out_7;
  //   fc = out_8; RDMEM = in_5; rst = in_6; WRMEM = in_4

  // Notes on the sheet:
  //   Random broj predstavlja vreme pristupa memoriji
  //   Brojac za generisanje random broja 
  //   Jedinica za generisanje function complete (fc) signala
  //   Brojac za dekrementiranje random broja
endmodule
